// Logisim project cachemem.circ as structural Verilog: 2 circuits, main circuit main
module main (
  output [7:0] dataout
);

  wire button_1_out, clock_1_out, not_1_out;
  wire [7:0] counter_1_q;
  wire [15:0] rom_1_data;

  Clock clock_1 (.out(clock_1_out));
  Button button_1 (.out(button_1_out));
  Counter counter_1 (.Q(counter_1_q), .clk(clock_1_out), .clr(button_1_out));  // open: load, D, count, carry
  ROM #(.dataWidth(16)) rom_1 (.addr(counter_1_q), .data(rom_1_data), .sel(1'b1));
  memorysystem memorysystem_1 (
    .addr({1'b0, rom_1_data[14:0]}), .Clock(clock_1_out), .Write(rom_1_data[15]), .Read(not_1_out),
    .dataout(dataout));  // open: datain, Reset
  not not_1 (not_1_out, rom_1_data[15]);
  Hex_Digit_Display hex_digit_display_1 (.value(dataout[7:4]));  // open: dp
  Hex_Digit_Display hex_digit_display_2 (.value(dataout[3:0]));  // open: dp

  // Notes on the sheet:
  //   Fake instructions
  //   R/W bit plus mem addresses
  //   Leading bit... 0=R, 1=W
  //   contents of rom_1 (hex, n*v repeats v):
  //   0 1 2 3 4 5 6 7 8008 8009 800a 800b 800c 800d 800e 800f
endmodule

module memorysystem (
  input  [15:0] addr,
  input  [7:0] datain,
  input  Clock,
  input  Write,
  input  Read,
  input  Reset,
  output [7:0] dataout
);

  RAM #(.addrWidth(2), .dataWidth(32), .bus("separate")) ram_1 (.addr(addr[5:4]));  // open: din, data, str, sel, clk, ld, clr
  RAM #(.addrWidth(2), .dataWidth(32), .bus("separate")) ram_2 (.addr(addr[5:4]));  // open: din, data, str, sel, clk, ld, clr
  RAM #(.addrWidth(16), .bus("separate")) ram_3 (
    .addr(addr), .din(datain), .str(Write), .sel(1'b1), .clk(Clock), .ld(Read), .clr(Reset));  // open: data
  RAM #(.addrWidth(2), .dataWidth(32), .bus("separate")) ram_4 (.addr(addr[5:4]));  // open: din, data, str, sel, clk, ld, clr
  RAM #(.addrWidth(2), .dataWidth(32), .bus("separate")) ram_5 (.addr(addr[5:4]));  // open: din, data, str, sel, clk, ld, clr

  // Notes on the sheet:
  //   Cache with block size of 16 and a tiny one at that with only FOUR cache lines
  //   RAM
endmodule
